// Logisim project Guia_0502.circ as structural Verilog: 1 circuit, main circuit main
module main (
  input  B,
  input  A,
  input  B_2,
  input  A_2,
  output out_5,
  output S
);

  wire and_1_out, and_2_out, and_3_out, and_4_out, not_1_out, not_2_out, not_3_out, not_4_out;

  not not_1 (not_1_out, A);
  and and_1 (and_1_out, B_2, B_2);
  not not_2 (not_2_out, and_1_out);
  and and_2 (and_2_out, A_2, A_2);
  not not_3 (not_3_out, and_2_out);
  and and_3 (and_3_out, not_3_out, not_3_out);
  not not_4 (not_4_out, and_3_out);
  or or_1 (out_5, B, not_1_out);
  not not_5 (S, and_4_out);
  and and_4 (and_4_out, not_2_out, not_4_out);

  // Notes on the sheet:
  //   X
endmodule
