// Logisim project Guia_0504.circ as structural Verilog: 1 circuit, main circuit main
module main (
  input  A,
  input  B,
  output out_3
);

  wire and_1_out, and_2_out, and_3_out, and_4_out, not_1_out, not_2_out, not_4_out;

  and and_1 (and_1_out, B, B);
  not not_1 (not_1_out, and_1_out);
  and and_2 (and_2_out, A, not_1_out);
  not not_2 (not_2_out, and_2_out);
  and and_3 (and_3_out, not_2_out, not_2_out);
  and and_4 (and_4_out, not_4_out, not_4_out);
  not not_3 (out_3, and_4_out);
  not not_4 (not_4_out, and_3_out);
endmodule
