// Logisim project Guia_0505.circ as structural Verilog: 1 circuit, main circuit main
module main (
  input  B,
  input  A,
  input  A_2,
  input  B_2,
  output out_5,
  output out_6
);

  wire and_1_out, and_2_out, not_1_out, not_2_out, not_3_out, not_4_out, not_5_out, not_6_out, not_7_out,
       not_8_out, not_9_out, not_10_out, not_11_out, not_12_out, not_13_out, not_16_out, not_17_out,
       not_18_out, or_1_out, or_2_out, or_3_out, or_4_out, or_5_out, or_6_out, or_7_out, or_8_out, or_9_out,
       or_10_out, or_11_out, or_12_out;

  not not_1 (not_1_out, A);
  and and_1 (and_1_out, not_1_out, not_3_out);
  not not_2 (not_2_out, and_1_out);
  not not_3 (not_3_out, A);
  and and_2 (and_2_out, A, A);
  not not_4 (not_4_out, and_2_out);
  or or_1 (or_1_out, A_2, A_2);
  not not_5 (not_5_out, or_1_out);
  or or_2 (or_2_out, not_5_out, not_5_out);
  not not_6 (not_6_out, or_2_out);
  or or_3 (or_3_out, not_6_out, not_12_out);
  not not_7 (not_7_out, or_3_out);
  not not_8 (not_8_out, not_2_out);
  not not_9 (not_9_out, or_4_out);
  or or_4 (or_4_out, not_8_out, not_10_out);
  not not_10 (not_10_out, not_4_out);
  or or_5 (or_5_out, B_2, B_2);
  not not_11 (not_11_out, or_5_out);
  or or_6 (or_6_out, not_11_out, not_11_out);
  not not_12 (not_12_out, or_6_out);
  or or_7 (or_7_out, not_7_out, not_18_out);
  not not_13 (not_13_out, or_7_out);
  or or_8 (or_8_out, not_13_out, not_13_out);
  not not_14 (out_6, or_8_out);
  or or_9 (or_9_out, not_9_out, not_9_out);
  not not_15 (out_5, or_9_out);
  or or_10 (or_10_out, B_2, B_2);
  or or_11 (or_11_out, A_2, A_2);
  not not_16 (not_16_out, or_10_out);
  not not_17 (not_17_out, or_11_out);
  or or_12 (or_12_out, not_17_out, not_16_out);
  not not_18 (not_18_out, or_12_out);

  assign B = A;

  // Notes on the sheet:
  //   xnor = 1 0 0 1
  //   0 1 1 0
  //   ~(a xnor b) = nor
endmodule
