// Logisim project Guia_13.circ as structural Verilog
module _1305 (
  input  Clear
);

  wire and_1_out, Clock_out, or_1_out, t_ff_1_q, t_ff_2_q, t_ff_2_qn, t_ff_3_q, t_ff_3_qn;

  Clock Clock (.out(Clock_out));
  or or_1 (or_1_out, Clear, and_1_out);
  // Probe on t_ff_1_q
  T_Flip_Flop t_ff_1 (.clk(t_ff_2_qn), .T(t_ff_2_qn), .Q(t_ff_1_q), .reset(or_1_out));  // open: Qn, preset
  and and_1 (and_1_out, t_ff_1_q, t_ff_2_q, t_ff_3_q);
  // Probe on t_ff_2_q
  T_Flip_Flop t_ff_2 (.clk(t_ff_3_qn), .T(t_ff_3_qn), .Q(t_ff_2_q), .Qn(t_ff_2_qn), .reset(or_1_out));  // open: preset
  T_Flip_Flop t_ff_3 (.clk(Clock_out), .T(Clock_out), .Q(t_ff_3_q), .Qn(t_ff_3_qn), .reset(or_1_out));  // open: preset
  // Probe on t_ff_3_q

  // Notes on the sheet:
  //   Contador Síncrono Módulo 7
endmodule

module _1306 (
  input  Input,
  input  Clear
);

  wire Clock_out, j_k_ff_1_q, j_k_ff_1_qn, j_k_ff_2_q, j_k_ff_2_qn, j_k_ff_3_q, j_k_ff_3_qn, j_k_ff_4_q,
       j_k_ff_4_qn, j_k_ff_5_q, j_k_ff_5_qn, j_k_ff_6_q, not_1_out, or_1_out;

  Clock Clock (.out(Clock_out));
  or or_1 (or_1_out, j_k_ff_6_q, Input);
  not not_1 (not_1_out, or_1_out);
  J_K_Flip_Flop j_k_ff_1 (
    .J(or_1_out), .clk(Clock_out), .K(not_1_out), .Q(j_k_ff_1_q), .Qn(j_k_ff_1_qn), .reset(Clear));  // open: preset
  J_K_Flip_Flop j_k_ff_2 (
    .J(j_k_ff_1_q), .clk(Clock_out), .K(j_k_ff_1_qn), .Q(j_k_ff_2_q), .Qn(j_k_ff_2_qn), .reset(Clear));  // open: preset
  J_K_Flip_Flop j_k_ff_3 (
    .J(j_k_ff_2_q), .clk(Clock_out), .K(j_k_ff_2_qn), .Q(j_k_ff_3_q), .Qn(j_k_ff_3_qn), .reset(Clear));  // open: preset
  J_K_Flip_Flop j_k_ff_4 (
    .J(j_k_ff_3_q), .clk(Clock_out), .K(j_k_ff_3_qn), .Q(j_k_ff_4_q), .Qn(j_k_ff_4_qn), .reset(Clear));  // open: preset
  // Probe on j_k_ff_1_q
  // Probe on j_k_ff_3_q
  // Probe on j_k_ff_4_q
  // Probe on j_k_ff_2_q
  J_K_Flip_Flop j_k_ff_5 (
    .J(j_k_ff_4_q), .clk(Clock_out), .K(j_k_ff_4_qn), .Q(j_k_ff_5_q), .Qn(j_k_ff_5_qn), .reset(Clear));  // open: preset
  // Probe on j_k_ff_6_q
  // Probe on j_k_ff_5_q
  J_K_Flip_Flop j_k_ff_6 (
    .J(j_k_ff_5_q), .clk(Clock_out), .K(j_k_ff_5_qn), .Q(j_k_ff_6_q), .reset(Clear));  // open: Qn, preset

  // Notes on the sheet:
  //   Contador em Anel de 6 bits
endmodule

module _1307 (
  input  Input,
  input  Clear
);

  wire Clock_out, j_k_ff_1_q, j_k_ff_1_qn, j_k_ff_2_q, j_k_ff_2_qn, j_k_ff_3_q, j_k_ff_3_qn, j_k_ff_4_q,
       j_k_ff_4_qn, j_k_ff_5_q, j_k_ff_5_qn, j_k_ff_6_q, j_k_ff_6_qn, not_1_out, or_1_out;

  Clock Clock (.out(Clock_out));
  or or_1 (or_1_out, Input, j_k_ff_6_qn);
  not not_1 (not_1_out, or_1_out);
  J_K_Flip_Flop j_k_ff_1 (
    .J(or_1_out), .clk(Clock_out), .K(not_1_out), .Q(j_k_ff_1_q), .Qn(j_k_ff_1_qn), .reset(Clear));  // open: preset
  J_K_Flip_Flop j_k_ff_2 (
    .J(j_k_ff_1_q), .clk(Clock_out), .K(j_k_ff_1_qn), .Q(j_k_ff_2_q), .Qn(j_k_ff_2_qn), .reset(Clear));  // open: preset
  J_K_Flip_Flop j_k_ff_3 (
    .J(j_k_ff_2_q), .clk(Clock_out), .K(j_k_ff_2_qn), .Q(j_k_ff_3_q), .Qn(j_k_ff_3_qn), .reset(Clear));  // open: preset
  J_K_Flip_Flop j_k_ff_4 (
    .J(j_k_ff_3_q), .clk(Clock_out), .K(j_k_ff_3_qn), .Q(j_k_ff_4_q), .Qn(j_k_ff_4_qn), .reset(Clear));  // open: preset
  // Probe on j_k_ff_1_q
  // Probe on j_k_ff_4_q
  // Probe on j_k_ff_2_q
  // Probe on j_k_ff_3_q
  J_K_Flip_Flop j_k_ff_5 (
    .J(j_k_ff_4_q), .clk(Clock_out), .K(j_k_ff_4_qn), .Q(j_k_ff_5_q), .Qn(j_k_ff_5_qn), .reset(Clear));  // open: preset
  // Probe on j_k_ff_5_q
  // Probe on j_k_ff_6_q
  J_K_Flip_Flop j_k_ff_6 (
    .J(j_k_ff_5_q), .clk(Clock_out), .K(j_k_ff_5_qn), .Q(j_k_ff_6_q), .Qn(j_k_ff_6_qn), .reset(Clear));  // open: preset

  // Notes on the sheet:
  //   Contador em Anel Torcido de 6 bits
endmodule
