// Logisim project q04.circ as structural Verilog: 1 circuit, main circuit main
module main (
);

  wire clock_1_out, j_k_ff_1_qn, not_1_out;

  Clock clock_1 (.out(clock_1_out));
  J_K_Flip_Flop j_k_ff_1 (.J(1'b1), .clk(clock_1_out), .K(1'b1), .Qn(j_k_ff_1_qn));  // open: Q, preset, reset
  not not_1 (not_1_out, j_k_ff_1_qn);
  J_K_Flip_Flop j_k_ff_2 (.J(j_k_ff_1_qn), .K(not_1_out));  // open: clk, Q, Qn, preset, reset
endmodule
