// Logisim project q07.circ as structural Verilog: 1 circuit, main circuit main
module main (
);

  wire and_1_out, clock_1_out, not_1_out, not_2_out, not_3_out, not_4_out;
  wire [5:0] counter_1_q;

  Counter #(.width(6), .max('h23)) counter_1 (
    .Q(counter_1_q), .clk(clock_1_out), .clr(and_1_out));  // open: load, D, count, carry, preset, down
  Clock clock_1 (.out(clock_1_out));
  not not_1 (not_1_out, counter_1_q[1]);
  not not_2 (not_2_out, counter_1_q[2]);
  not not_3 (not_3_out, counter_1_q[3]);
  not not_4 (not_4_out, counter_1_q[4]);
  and and_1 (and_1_out, counter_1_q[0], not_1_out, not_2_out, not_3_out, not_4_out, counter_1_q[5]);
endmodule
